// Logisim project P0_L0_grf.circ as structural Verilog
module memory (
  input  [31:0] in_1,
  input  in_2,
  input  in_3,
  input  in_4,
  output [31:0] out_5
);

  wire [31:0] next;

  Register #(.width(32)) register_1 (.D(next), .Q(out_5), .clk(in_3), .clr(in_4));  // open: en
  Multiplexer #(.width(32)) multiplexer_1 (.in0(out_5), .in1(in_1), .out(next), .sel(in_2));  // open: en

  // Other names for the same wires on the sheet: clk = in_3; in_check = in_2; in_data[31:0] = in_1;
  //   last[31:0] = out_5; reset = in_4
endmodule

module grf (
  input  in_1,
  input  [4:0] in_2,
  input  in_3,
  input  [4:0] in_4,
  input  [4:0] in_5,
  input  in_6,
  input  [31:0] in_7,
  output [31:0] out_8,
  output [31:0] out_9
);

  wire in_check0, in_check1, in_check2, in_check3, in_check4, in_check5, in_check6, in_check7, in_check8,
       in_check9, in_check10, in_check11, in_check12, in_check13, in_check14, in_check15, in_check16,
       in_check17, in_check18, in_check19, in_check20, in_check21, in_check22, in_check23, in_check24,
       in_check25, in_check26, in_check27, in_check28, in_check29, in_check30, in_check31;
  wire [31:0] out0, out1, out2, out3, out4, out5, out6, out7, out8, out9, out10, out11, out12, out13, out14,
       out15, out16, out17, out18, out19, out20, out21, out22, out23, out24, out25, out26, out27, out28,
       out29, out30, out31;

  Demultiplexer #(.select(5)) demultiplexer_1 (
    .out0(in_check0), .out1(in_check1), .out2(in_check2), .out3(in_check3), .out4(in_check4),
    .out5(in_check5), .out6(in_check6), .out7(in_check7), .out8(in_check8), .out9(in_check9),
    .out10(in_check10), .out11(in_check11), .out12(in_check12), .out13(in_check13), .out14(in_check14),
    .out15(in_check15), .out16(in_check16), .out17(in_check17), .out18(in_check18), .out19(in_check19),
    .out20(in_check20), .out21(in_check21), .out22(in_check22), .out23(in_check23), .out24(in_check24),
    .out25(in_check25), .out26(in_check26), .out27(in_check27), .out28(in_check28), .out29(in_check29),
    .out30(in_check30), .out31(in_check31), .in(in_6), .sel(in_5));  // open: en
  memory memory_1 (.in_1({32{1'b0}}), .in_2(in_check0), .in_3(in_1), .in_4(in_3), .out_5(out0));
  memory memory_2 (.in_1(in_7), .in_2(in_check1), .in_3(in_1), .in_4(in_3), .out_5(out1));
  memory memory_3 (.in_1(in_7), .in_2(in_check2), .in_3(in_1), .in_4(in_3), .out_5(out2));
  memory memory_4 (.in_1(in_7), .in_2(in_check3), .in_3(in_1), .in_4(in_3), .out_5(out3));
  memory memory_5 (.in_1(in_7), .in_2(in_check4), .in_3(in_1), .in_4(in_3), .out_5(out4));
  memory memory_6 (.in_1(in_7), .in_2(in_check5), .in_3(in_1), .in_4(in_3), .out_5(out5));
  memory memory_7 (.in_1(in_7), .in_2(in_check6), .in_3(in_1), .in_4(in_3), .out_5(out6));
  memory memory_8 (.in_1(in_7), .in_2(in_check7), .in_3(in_1), .in_4(in_3), .out_5(out7));
  memory memory_9 (.in_1(in_7), .in_2(in_check8), .in_3(in_1), .in_4(in_3), .out_5(out8));
  memory memory_10 (.in_1(in_7), .in_2(in_check9), .in_3(in_1), .in_4(in_3), .out_5(out9));
  memory memory_11 (.in_1(in_7), .in_2(in_check10), .in_3(in_1), .in_4(in_3), .out_5(out10));
  memory memory_12 (.in_1(in_7), .in_2(in_check11), .in_3(in_1), .in_4(in_3), .out_5(out11));
  memory memory_13 (.in_1(in_7), .in_2(in_check12), .in_3(in_1), .in_4(in_3), .out_5(out12));
  memory memory_14 (.in_1(in_7), .in_2(in_check13), .in_3(in_1), .in_4(in_3), .out_5(out13));
  memory memory_15 (.in_1(in_7), .in_2(in_check14), .in_3(in_1), .in_4(in_3), .out_5(out14));
  memory memory_16 (.in_1(in_7), .in_2(in_check15), .in_3(in_1), .in_4(in_3), .out_5(out15));
  Multiplexer #(.select(5), .width(32)) multiplexer_1 (
    .in0(out0), .in1(out1), .in2(out2), .in3(out3), .in4(out4), .in5(out5), .in6(out6), .in7(out7),
    .in8(out8), .in9(out9), .in10(out10), .in11(out11), .in12(out12), .in13(out13), .in14(out14),
    .in15(out15), .in16(out16), .in17(out17), .in18(out18), .in19(out19), .in20(out20), .in21(out21),
    .in22(out22), .in23(out23), .in24(out24), .in25(out25), .in26(out26), .in27(out27), .in28(out28),
    .in29(out29), .in30(out30), .in31(out31), .out(out_8), .sel(in_2));  // open: en
  Multiplexer #(.select(5), .width(32)) multiplexer_2 (
    .in0(out0), .in1(out1), .in2(out2), .in3(out3), .in4(out4), .in5(out5), .in6(out6), .in7(out7),
    .in8(out8), .in9(out9), .in10(out10), .in11(out11), .in12(out12), .in13(out13), .in14(out14),
    .in15(out15), .in16(out16), .in17(out17), .in18(out18), .in19(out19), .in20(out20), .in21(out21),
    .in22(out22), .in23(out23), .in24(out24), .in25(out25), .in26(out26), .in27(out27), .in28(out28),
    .in29(out29), .in30(out30), .in31(out31), .out(out_9), .sel(in_4));  // open: en
  memory memory_17 (.in_1(in_7), .in_2(in_check16), .in_3(in_1), .in_4(in_3), .out_5(out16));
  memory memory_18 (.in_1(in_7), .in_2(in_check17), .in_3(in_1), .in_4(in_3), .out_5(out17));
  memory memory_19 (.in_1(in_7), .in_2(in_check18), .in_3(in_1), .in_4(in_3), .out_5(out18));
  memory memory_20 (.in_1(in_7), .in_2(in_check19), .in_3(in_1), .in_4(in_3), .out_5(out19));
  memory memory_21 (.in_1(in_7), .in_2(in_check20), .in_3(in_1), .in_4(in_3), .out_5(out20));
  memory memory_22 (.in_1(in_7), .in_2(in_check21), .in_3(in_1), .in_4(in_3), .out_5(out21));
  memory memory_23 (.in_1(in_7), .in_2(in_check22), .in_3(in_1), .in_4(in_3), .out_5(out22));
  memory memory_24 (.in_1(in_7), .in_2(in_check23), .in_3(in_1), .in_4(in_3), .out_5(out23));
  memory memory_25 (.in_1(in_7), .in_2(in_check24), .in_3(in_1), .in_4(in_3), .out_5(out24));
  memory memory_26 (.in_1(in_7), .in_2(in_check25), .in_3(in_1), .in_4(in_3), .out_5(out25));
  memory memory_27 (.in_1(in_7), .in_2(in_check26), .in_3(in_1), .in_4(in_3), .out_5(out26));
  memory memory_28 (.in_1(in_7), .in_2(in_check27), .in_3(in_1), .in_4(in_3), .out_5(out27));
  memory memory_29 (.in_1(in_7), .in_2(in_check28), .in_3(in_1), .in_4(in_3), .out_5(out28));
  memory memory_30 (.in_1(in_7), .in_2(in_check29), .in_3(in_1), .in_4(in_3), .out_5(out29));
  memory memory_31 (.in_1(in_7), .in_2(in_check30), .in_3(in_1), .in_4(in_3), .out_5(out30));
  memory memory_32 (.in_1(in_7), .in_2(in_check31), .in_3(in_1), .in_4(in_3), .out_5(out31));

  // Other names for the same wires on the sheet: A1[4:0] = in_2; A2[4:0] = in_4; A3[4:0] = in_5; clk = in_1;
  //   RD1[31:0] = out_8; RD2[31:0] = out_9; reset = in_3; WD[31:0] = in_7; WE = in_6
endmodule
