// Logisim project automation.circ as structural Verilog: 1 circuit, main circuit main
module main (
);

  wire undriven, undriven_2, undriven_3;
  wire [7:0] in1, in2, in3, in4, in5, in6, in7, in8, in9, in10, out1, out2, out3, out4, out5, out6, out7,
       out8, out9, out10;

  Register register_1 (.D(in1), .en(undriven), .Q(out1), .clk(undriven_2), .clr(undriven_3));
  Register register_2 (.D(in1), .en(undriven), .Q(out1), .clk(undriven_2), .clr(undriven_3));
  Register register_3 (.D(in2), .Q(out2));  // open: en, clk, clr
  Register register_4 (.D(in3), .Q(out3));  // open: en, clk, clr
  Register register_5 (.D(in4), .Q(out4));  // open: en, clk, clr
  Register register_6 (.D(in5), .Q(out5));  // open: en, clk, clr
  Register register_7 (.D(in6), .Q(out6));  // open: en, clk, clr
  Register register_8 (.D(in7), .Q(out7));  // open: en, clk, clr
  Register register_9 (.D(in8), .Q(out8));  // open: en, clk, clr
  Register register_10 (.D(in9), .Q(out9));  // open: en, clk, clr
  Register register_11 (.D(in10), .Q(out10));  // open: en, clk, clr
endmodule
